# Fritzing sketch doorGate-RFID (saved by Fritzing 0.9.3b)
breadboards: 1

parts:
  Componente1 = Arduino Uno (Rev3)
  Componente2 = RFID-RC522-v2
  J1 = Piezo Speaker
  JP1 = Header 2 [package=molex-1x2_lock]
  R1 = Resistor [tolerance=±5% resistance=220 package=THT]
  S1 = Momentary Switch [package=ksa_sealed_tac_switch]
  R2 = Resistor [tolerance=±5% resistance=220 package=THT]
  LED1 = LED - 3mm [color="Red (633nm)" package="3 mm [THT]"]
  R3 = Resistor [tolerance=±5% resistance=220 package=THT]
  LED2 = LED - 3mm [color="Green (565nm)" package="3 mm [THT]"]
  R4 = Resistor [tolerance=±5% resistance=220 package=THT]
  Q1 = NPN-Transistor [package="SOT-23 [SMD]"]
  R5 = Resistor [tolerance=±5% resistance=1.5k package=THT]
  OMRON1 = OMRON PCB Power Relay – G5LE [part_number="G5LE-1\n" package=THT]
  HLK-PM1 = HLK-PM12 [part_number=HLK-PM12]
  D1 = Diode [package=diode-1n4001]
  IC1 = Voltage Regulator [package=to220-igo]
  C1 = Capacitor Polarized [package=cpol-radial-10uf-25v]
  C2 = Capacitor Polarized [package=cpol-radial-10uf-25v]

nets:
  N1: Componente1.D9_PWM, Componente2.RST
  N2: Componente1.D10_PWM/SS, Componente2.SDA
  N3: Componente1.D11_PWM/MOSI, Componente2.MOSI
  N4: Componente1.D12/MISO, Componente2.MISO
  N5: Componente1.D13/SCK, Componente2.SCK
  GND: Componente1.GND, Componente2.GND, J1.pin1, R1.Pin_0, R2.Pin_1, R3.Pin_0, R4.Pin_0, Q1.1, HLK-PM1.-Vo, IC1.IN, C1.+, C2.-
  N6: Componente1.D2, S1.1, R2.Pin_0
  N7: Componente1.D3_PWM, LED1.anode
  N8: Componente1.D4, JP1.1, R1.Pin_1
  N9: Componente1.D5_PWM, LED2.anode
  N10: Componente1.D6_PWM, R5.Pin_1
  N11: Componente1.D7, J1.pin2
  5V: Componente1.5V, Componente2.3.3V, JP1.2, S1.3, IC1.OUT
  N12: LED1.cathode, R3.Pin_1
  N13: LED2.cathode, R4.Pin_1
  N14: Q1.2, OMRON1.COIL2
  N15: Q1.0, R5.Pin_0
  N16: OMRON1.COIL1, OMRON1.C, HLK-PM1.+Vo, D1.C, IC1.GND, C2.+

notes:
  470nF
  100nF
  BC547
  7805
  12v
  JUMPER
  BUZZER

custom parts:
  RFID-RC522-v2: A simple China made RFID-RC522 Reader; do check the pin labels, as this is a MFRC522 based clone.
